// Digital circuit sr_ff.dig as structural Verilog
module sr_ff (
  input  S,
  input  R,
  input  Clk,
  output Q,
  output Qo
);

  wire and_1_out, and_2_out;

  and and_1 (and_1_out, S, Clk);
  and and_2 (and_2_out, Clk, R);
  nor nor_1 (Q, and_1_out, Qo);
  nor nor_2 (Qo, Q, and_2_out);
endmodule
